// Logisim project Logisim Project1.circ as structural Verilog: 12 circuits, main circuit Basic Gates
module Basic_Gates (
  input  A,
  input  B,
  output AandB,
  output AorB,
  output notA
);

  and and_1 (AandB, A, B);
  or or_1 (AorB, A, B);
  not not_1 (notA, A);
endmodule

module _1bitMUX (
  input  A,
  input  B,
  input  Select,
  output out_4
);

  wire and_1_out, and_2_out, not_1_out;

  not not_1 (not_1_out, Select);
  and and_1 (and_1_out, A, Select);
  and and_2 (and_2_out, B, not_1_out);
  or or_1 (out_4, and_1_out, and_2_out);
endmodule

module _3bitMUX (
  input  [2:0] in_1,
  input  [2:0] in_2,
  input  in_3,
  output [2:0] out_4,
  output [2:0] out_5
);

  wire [2:0] and_1_out, and_2_out;
  wire [2:2] not_1_out;

  Multiplexer #(.width(3), .enable("false")) multiplexer_1 (.in0(in_1), .in1(in_2), .out(out_5), .sel(in_3));
  not not_1 (not_1_out[2], in_3);
  assign and_1_out = in_1 & {3{not_1_out[2]}};  // AND_Gate and_1, 3 bits wide
  assign and_2_out = in_2 & {3{in_3}};  // AND_Gate and_2, 3 bits wide
  assign out_4 = and_1_out | and_2_out;  // OR_Gate or_1, 3 bits wide
endmodule

// RF
module Register (
  input  [31:0] Data,
  input  [4:0] RD,
  input  [4:0] RS,
  input  [4:0] RT,
  input  Clock,
  input  Reset,
  output [31:0] RS_Value,
  output [31:0] RT_Value
);

  wire demultiplexer_1_out0, demultiplexer_1_out1, demultiplexer_1_out2, demultiplexer_1_out3,
       demultiplexer_2_out0, demultiplexer_2_out1, demultiplexer_2_out2, demultiplexer_2_out3,
       demultiplexer_3_out0, demultiplexer_3_out1, demultiplexer_3_out2, demultiplexer_3_out3;
  wire [31:0] rf_subpart_1_rsvalue, rf_subpart_1_rtvalue, rf_subpart_2_rsvalue, rf_subpart_2_rtvalue,
       rf_subpart_3_rsvalue, rf_subpart_3_rtvalue, rf_subpart_4_rsvalue, rf_subpart_4_rtvalue;

  Demultiplexer #(.select(2), .enable("false")) demultiplexer_1 (
    .out0(demultiplexer_1_out0), .out1(demultiplexer_1_out1), .out2(demultiplexer_1_out2),
    .out3(demultiplexer_1_out3), .in(1'b1), .sel(RD[4:3]));
  Demultiplexer #(.select(2), .enable("false")) demultiplexer_2 (
    .out0(demultiplexer_2_out0), .out1(demultiplexer_2_out1), .out2(demultiplexer_2_out2),
    .out3(demultiplexer_2_out3), .in(1'b1), .sel(RS[4:3]));
  Demultiplexer #(.select(2), .enable("false")) demultiplexer_3 (
    .out0(demultiplexer_3_out0), .out1(demultiplexer_3_out1), .out2(demultiplexer_3_out2),
    .out3(demultiplexer_3_out3), .in(1'b1), .sel(RT[4:3]));
  RF_subpart rf_subpart_1 (
    .Data(Data), .RD(RD[2:0]), .RS(RS[2:0]), .RT(RT[2:0]), .EnableRD(demultiplexer_1_out0),
    .EnableRS(demultiplexer_2_out0), .EnableRT(demultiplexer_3_out0), .Clock(Clock), .Reset(Reset),
    .RSValue(rf_subpart_1_rsvalue), .RTValue(rf_subpart_1_rtvalue));
  RF_subpart rf_subpart_2 (
    .Data(Data), .RD(RD[2:0]), .RS(RS[2:0]), .RT(RT[2:0]), .EnableRD(demultiplexer_1_out1),
    .EnableRS(demultiplexer_2_out1), .EnableRT(demultiplexer_3_out1), .Clock(Clock), .Reset(Reset),
    .RSValue(rf_subpart_2_rsvalue), .RTValue(rf_subpart_2_rtvalue));
  RF_subpart rf_subpart_3 (
    .Data(Data), .RD(RD[2:0]), .RS(RS[2:0]), .RT(RT[2:0]), .EnableRD(demultiplexer_1_out2),
    .EnableRS(demultiplexer_2_out2), .EnableRT(demultiplexer_3_out2), .Clock(Clock), .Reset(Reset),
    .RSValue(rf_subpart_3_rsvalue), .RTValue(rf_subpart_3_rtvalue));
  RF_subpart rf_subpart_4 (
    .Data(Data), .RD(RD[2:0]), .RS(RS[2:0]), .RT(RT[2:0]), .EnableRD(demultiplexer_1_out3),
    .EnableRS(demultiplexer_2_out3), .EnableRT(demultiplexer_3_out3), .Clock(Clock), .Reset(Reset),
    .RSValue(rf_subpart_4_rsvalue), .RTValue(rf_subpart_4_rtvalue));
  assign RS_Value = rf_subpart_1_rsvalue | rf_subpart_2_rsvalue | rf_subpart_3_rsvalue | rf_subpart_4_rsvalue;  // OR_Gate RS, 32 bits wide
  assign RT_Value = rf_subpart_1_rtvalue | rf_subpart_2_rtvalue | rf_subpart_3_rtvalue | rf_subpart_4_rtvalue;  // OR_Gate RT, 32 bits wide
endmodule

module FlipFlop (
  input  in_1,
  input  in_2,
  output out_3,
  output out_4
);

  nor nor_1 (out_3, in_1, out_4);
  nor nor_2 (out_4, out_3, in_2);
endmodule

module PC (
  input  Clock,
  input  Reset,
  output out_3,
  output [31:0] out_4
);

  wire [31:0] adder_1_out, multiplexer_1_out, register_1_q;

  Multiplexer #(.width(32), .enable("false")) multiplexer_1 (
    .in0(adder_1_out), .in1({{6{1'b0}}, out_4[25:0]}), .out(multiplexer_1_out), .sel(out_3));
  Register_part #(.width(32)) register_1 (
    .D(multiplexer_1_out), .Q(register_1_q), .clk(Clock), .clr(Reset));  // open: en
  Adder #(.width(32)) adder_1 (.a(register_1_q), .b(32'h1), .out(adder_1_out));  // open: cin, cout
  and and_1 (out_3, ~out_4[26], out_4[27], ~out_4[28], ~out_4[29], ~out_4[30], ~out_4[31]);  // AND_Gate
  RAM #(.addrWidth(24), .dataWidth(32)) ram_1 (
    .addr(register_1_q[23:0]), .data(out_4), .clk(Clock));  // open: sel, ld, clr
endmodule

module MEM (
  input  [23:0] in_1,
  input  [31:0] in_2,
  input  in_3,
  input  in_4,
  output [31:0] out_5
);

  wire not_1_out;

  not not_1 (not_1_out, in_3);
  RAM #(.addrWidth(24), .dataWidth(32), .bus("separate")) ram_1 (
    .addr(in_1), .din(in_2), .data(out_5), .str(in_3), .clk(in_4), .ld(not_1_out));  // open: sel, clr
endmodule

module ALU (
  input  [31:0] A,
  input  [31:0] b,
  input  [5:0] FunctCode,
  output [31:0] Output
);

  wire [0:0] or_2_out;
  wire [31:0] adder_1_out, and_1_out, or_1_out, subtractor_1_out;

  Adder #(.width(32)) adder_1 (.a(A), .b(b), .out(adder_1_out));  // open: cin, cout
  Subtractor #(.width(32)) subtractor_1 (.a(A), .b(b), .out(subtractor_1_out));  // open: bin, bout
  assign and_1_out = A & b;  // AND_Gate and_1, 32 bits wide
  assign or_1_out = A | b;  // OR_Gate or_1, 32 bits wide
  Multiplexer #(.select(2), .width(32), .enable("false")) multiplexer_1 (
    .in0(adder_1_out), .in1(subtractor_1_out), .in2(and_1_out), .in3(or_1_out), .out(Output),
    .sel({FunctCode[2], or_2_out[0]}));
  or or_2 (or_2_out[0], FunctCode[0], FunctCode[1]);
endmodule

// RFSubpart
module RF_subpart (
  input  [31:0] Data,
  input  [2:0] RD,
  input  [2:0] RS,
  input  [2:0] RT,
  input  EnableRD,
  input  EnableRS,
  input  EnableRT,
  input  Clock,
  input  Reset,
  output [31:0] RSValue,
  output [31:0] RTValue
);

  wire demultiplexer_1_out0, demultiplexer_1_out1, demultiplexer_1_out2, demultiplexer_1_out3,
       demultiplexer_1_out4, demultiplexer_1_out5, demultiplexer_1_out6, demultiplexer_1_out7;
  wire [31:0] multiplexer_1_out, multiplexer_2_out, register_1_q, register_2_q, register_3_q, register_4_q,
       register_5_q, register_6_q, register_7_q, register_8_q;

  Demultiplexer #(.select(3)) demultiplexer_1 (
    .out0(demultiplexer_1_out0), .out1(demultiplexer_1_out1), .out2(demultiplexer_1_out2),
    .out3(demultiplexer_1_out3), .out4(demultiplexer_1_out4), .out5(demultiplexer_1_out5),
    .out6(demultiplexer_1_out6), .out7(demultiplexer_1_out7), .in(EnableRD), .sel(RD), .en(1'b1));
  Register_part #(.width(32)) register_1 (
    .D(Data), .en(demultiplexer_1_out0), .Q(register_1_q), .clk(Clock), .clr(Reset));
  Register_part #(.width(32)) register_2 (
    .D(Data), .en(demultiplexer_1_out1), .Q(register_2_q), .clk(Clock), .clr(Reset));
  Register_part #(.width(32)) register_3 (
    .D(Data), .en(demultiplexer_1_out2), .Q(register_3_q), .clk(Clock), .clr(Reset));
  Register_part #(.width(32)) register_4 (
    .D(Data), .en(demultiplexer_1_out3), .Q(register_4_q), .clk(Clock), .clr(Reset));
  Register_part #(.width(32)) register_5 (
    .D(Data), .en(demultiplexer_1_out4), .Q(register_5_q), .clk(Clock), .clr(Reset));
  Register_part #(.width(32)) register_6 (
    .D(Data), .en(demultiplexer_1_out5), .Q(register_6_q), .clk(Clock), .clr(Reset));
  Register_part #(.width(32)) register_7 (
    .D(Data), .en(demultiplexer_1_out6), .Q(register_7_q), .clk(Clock), .clr(Reset));
  Register_part #(.width(32)) register_8 (
    .D(Data), .en(demultiplexer_1_out7), .Q(register_8_q), .clk(Clock), .clr(Reset));
  Multiplexer #(.select(3), .width(32)) multiplexer_1 (
    .in0(register_1_q), .in1(register_2_q), .in2(register_3_q), .in3(register_4_q), .in4(register_5_q),
    .in5(register_6_q), .in6(register_7_q), .in7(register_8_q), .out(multiplexer_1_out), .sel(RS),
    .en(EnableRS));
  Multiplexer #(.select(3), .width(32)) multiplexer_2 (
    .in0(register_1_q), .in1(register_2_q), .in2(register_3_q), .in3(register_4_q), .in4(register_5_q),
    .in5(register_6_q), .in6(register_7_q), .in7(register_8_q), .out(multiplexer_2_out), .sel(RT),
    .en(EnableRT));
  Multiplexer #(.width(32), .enable("false")) multiplexer_3 (
    .in0({32{1'b0}}), .in1(multiplexer_1_out), .out(RSValue), .sel(EnableRS));
  Multiplexer #(.width(32), .enable("false")) multiplexer_4 (
    .in0({32{1'b0}}), .in1(multiplexer_2_out), .out(RTValue), .sel(EnableRT));
endmodule

module CPU_Circuit (
  input  in_1
);

  wire and_1_out, clock_1_out;
  wire [4:0] multiplexer_1_out;
  wire [5:0] multiplexer_2_out;
  wire [31:0] alu_1_output, mem_1_out_5, multiplexer_3_out, multiplexer_4_out, pc_1_out_4,
       register_1_rs_value, register_1_rt_value;

  PC pc_1 (.Clock(clock_1_out), .Reset(in_1), .out_4(pc_1_out_4));  // open: out_3
  Clock clock_1 (.out(clock_1_out));
  Register register_1 (
    .Data(multiplexer_4_out), .RD(multiplexer_1_out), .RS(pc_1_out_4[25:21]), .RT(pc_1_out_4[20:16]),
    .Clock(clock_1_out), .Reset(in_1), .RS_Value(register_1_rs_value), .RT_Value(register_1_rt_value));
  Multiplexer #(.width(5), .enable("false")) multiplexer_1 (
    .in0(pc_1_out_4[15:11]), .in1(pc_1_out_4[20:16]), .out(multiplexer_1_out), .sel(and_1_out));
  and and_1 (and_1_out, pc_1_out_4[31], ~pc_1_out_4[29]);  // AND_Gate
  Multiplexer #(.width(6), .enable("false")) multiplexer_2 (
    .in0(pc_1_out_4[5:0]), .in1(6'b100000), .out(multiplexer_2_out), .sel(pc_1_out_4[31]));
  Multiplexer #(.width(32), .enable("false")) multiplexer_3 (
    .in0(register_1_rt_value), .in1({{16{1'b0}}, pc_1_out_4[15:0]}), .out(multiplexer_3_out),
    .sel(pc_1_out_4[31]));
  Multiplexer #(.width(32), .enable("false")) multiplexer_4 (
    .in0(alu_1_output), .in1(mem_1_out_5), .out(multiplexer_4_out), .sel(pc_1_out_4[31]));
  ALU alu_1 (.A(register_1_rs_value), .b(multiplexer_3_out), .FunctCode(multiplexer_2_out), .Output(alu_1_output));
  MEM mem_1 (
    .in_1(alu_1_output[23:0]), .in_2(register_1_rt_value), .in_3(pc_1_out_4[29]), .in_4(clock_1_out),
    .out_5(mem_1_out_5));
endmodule

module Name (
  input  Enable,
  input  Clock,
  input  in_3,
  input  in_4,
  output out_5,
  output [7:0] out_6,
  output out_7,
  output out_8,
  output [4:0] out_9,
  output out_10
);

  wire clock_1_out;
  wire [2:0] register_1_q;

  Multiplexer #(.select(2), .width(8), .enable("false")) multiplexer_1 (
    .in0(8'h45), .in1(8'h48), .in2(8'h49), .in3(8'h4e), .out(out_6), .sel({in_3, in_4}));
  Register_part register_1 (.D(out_6), .en(Enable), .Q({out_9, register_1_q}), .clk(clock_1_out));  // open: clr
  Clock clock_1 (.out(clock_1_out));
  and M (out_5, ~register_1_q[0], ~register_1_q[1], ~register_1_q[2]);  // AND_Gate
  and A (out_7, register_1_q[0], ~register_1_q[1], register_1_q[2]);  // AND_Gate
  and R (out_8, register_1_q[0], ~register_1_q[1], ~register_1_q[2]);  // AND_Gate
  and K (out_10, ~register_1_q[0], register_1_q[1], register_1_q[2]);  // AND_Gate
endmodule

module Name_Mystery_Circuit (
  input  _0,
  input  _1,
  input  _2,
  input  _3,
  output _0_2,
  output _1_2
);
endmodule
